// Logisim project Processor.circ as structural Verilog: 5 circuits, main circuit Processor
module Processor (
);

  wire clock_1_out, not_1_out;
  wire [3:0] func_q, multiplexer_3_out, multiplexer_5_out, oppselector2_1_out_2, sll1_1_out_2, sll1_2_out_2;
  wire [4:0] A_q, mips_alu_1_p7, multiplexer_1_out, multiplexer_4_out, registerfile_1_p4, Rw_q, shamt_q;
  wire [5:0] Op_q;
  wire [5:4] func_q_2;
  wire [15:0] Imm_q;
  wire [26:0] A_q_2;
  wire [31:0] B_2_q, B_q, bit_extender_1_out, IF_ID_q, mips_alu_1_p6, mipsprogramrom_1_p2, multiplexer_2_out,
       pc_4_2_new, PC_q, registerfile_1_p1, registerfile_1_p7, registerfile_1_p8;

  Register #(.width(32)) PC (.D(pc_4_2_new), .Q(PC_q), .clk(clock_1_out));  // open: en, clr
  PC_4 pc_4_1 ();  // open: Old, New
  Clock clock_1 (.out(clock_1_out));
  PC_4 pc_4_2 (.Old(PC_q), .New(pc_4_2_new));
  // MIPSProgramROM mipsprogramrom_1: pin names not known; wires that end beside it: PC_q, mipsprogramrom_1_p2
  Register #(.width(32)) IF_ID (.D(mipsprogramrom_1_p2), .Q(IF_ID_q), .clk(clock_1_out));  // open: en, clr
  // Probe on IF_ID_q[20:0]
  // RegisterFile registerfile_1: pin names not known; wires that end beside it: registerfile_1_p1, clock_1_out, clock_1_out, registerfile_1_p4, IF_ID_q[25:21], IF_ID_q[20:16], registerfile_1_p7, registerfile_1_p8
  Register #(.width(32)) A (.D(registerfile_1_p7), .Q({A_q_2, A_q}), .clk(clock_1_out));  // open: en, clr
  Register #(.width(32)) B (.D(registerfile_1_p8), .Q(B_q), .clk(clock_1_out));  // open: en, clr
  Register #(.width(16)) Imm (.D(IF_ID_q[15:0]), .Q(Imm_q), .clk(clock_1_out));  // open: en, clr
  Register #(.width(5)) Rw (.D(multiplexer_1_out), .Q(Rw_q), .clk(clock_1_out));  // open: en, clr
  Multiplexer #(.width(5), .enable("false")) multiplexer_1 (
    .in0(IF_ID_q[15:11]), .in1(IF_ID_q[20:16]), .out(multiplexer_1_out), .sel(IF_ID_q[29]));
  Register #(.width(6)) Op (.D(IF_ID_q[31:26]), .Q(Op_q), .clk(clock_1_out));  // open: en, clr
  Register #(.width(5)) shamt (.D(IF_ID_q[10:6]), .Q(shamt_q), .clk(clock_1_out));  // open: en, clr
  Register #(.width(6)) func (.D(IF_ID_q[5:0]), .Q({func_q_2, func_q}), .clk(clock_1_out));  // open: en, clr
  assign bit_extender_1_out = {{16{Imm_q[15]}}, Imm_q};  // Bit_Extender bit_extender_1
  SLL1 sll1_1 (.in_1(Op_q[3:0]), .out_2(sll1_1_out_2));
  SLL1 sll1_2 (.in_1(func_q), .out_2(sll1_2_out_2));
  Oppselector2 oppselector2_1 (.out_2(oppselector2_1_out_2), .in_1(func_q));
  Multiplexer #(.width(32), .enable("false")) multiplexer_2 (
    .in0(B_q), .in1(bit_extender_1_out), .out(multiplexer_2_out), .sel(Op_q[3]));
  Multiplexer #(.width(4)) multiplexer_3 (
    .in0(oppselector2_1_out_2), .in1(sll1_2_out_2), .out(multiplexer_3_out), .sel(func_q_2[5]));  // open: en
  not not_1 (not_1_out, func_q[2]);
  Multiplexer #(.width(5), .enable("false")) multiplexer_4 (
    .in0(A_q), .in1(shamt_q), .out(multiplexer_4_out), .sel(not_1_out));
  Multiplexer #(.width(4)) multiplexer_5 (
    .in0(multiplexer_3_out), .in1(sll1_1_out_2), .out(multiplexer_5_out), .sel(Op_q[3]));  // open: en
  // Probe on mips_alu_1_p6
  // Mips_ALU mips_alu_1: pin names not known; wires that end beside it: shamt_q, {A_q_2, A_q}, multiplexer_2_out, multiplexer_5_out, multiplexer_4_out, mips_alu_1_p6, mips_alu_1_p7
  Register #(.width(32)) B_2 (.D(mips_alu_1_p6), .Q(B_2_q), .clk(clock_1_out));  // open: en, clr
  Register #(.width(5)) Rw_2 (.D(Rw_q), .Q(mips_alu_1_p7), .clk(clock_1_out));  // open: en, clr
  Register #(.width(32)) B_3 (.D(B_2_q), .Q(registerfile_1_p1), .clk(clock_1_out));  // open: en, clr
  Register #(.width(5)) Rw_3 (.D(mips_alu_1_p7), .Q(registerfile_1_p4), .clk(clock_1_out));  // open: en, clr
  // LCD_Video lcd_video_1: pin names not known
endmodule

module PC_4 (
  input  [31:0] Old,
  output [31:0] New
);

  // Incrementer incrementer_1: pin names not known; wires that end beside it: Old[31:2], New[31:2]

  assign New[1:0] = Old[1:0];
endmodule

module SLL1 (
  input  [3:0] in_1,
  output [3:0] out_2
);

  wire not_1_out;

  and and_1 (out_2[0], in_1[3], not_1_out);
  not not_1 (not_1_out, in_1[3]);

  assign out_2[3:1] = in_1[2:0];
endmodule

module Oppselect (
  input  [3:0] in_1,
  output [3:0] out_2
);

  wire and_2_out, and_3_out, and_5_out, not_1_out, not_2_out, not_3_out, not_4_out, not_5_out, not_6_out,
       not_7_out;

  and and_1 (out_2[3], in_1[3], not_1_out);
  not not_1 (not_1_out, in_1[2]);
  not not_2 (not_2_out, in_1[2]);
  and and_2 (and_2_out, not_2_out, not_3_out);
  not not_3 (not_3_out, in_1[1]);
  not not_4 (not_4_out, in_1[3]);
  and and_3 (and_3_out, not_4_out, in_1[1]);
  and and_4 (out_2[1], in_1[3], not_5_out, in_1[0]);
  not not_5 (not_5_out, in_1[2]);
  not not_6 (not_6_out, in_1[2]);
  not not_7 (not_7_out, in_1[3]);
  and and_5 (and_5_out, not_7_out, in_1[0]);
  or or_1 (out_2[2], and_2_out, and_3_out);
  or or_2 (out_2[0], not_6_out, and_5_out);
endmodule

module Oppselector2 (
  input  [3:0] in_1,
  output [3:0] out_2
);

  wire not_1_out, not_2_out, not_3_out;

  and and_1 (out_2[3], in_1[3], not_1_out);
  not not_1 (not_1_out, in_1[2]);
  not not_2 (not_2_out, in_1[3]);
  and and_2 (out_2[2], not_2_out, in_1[1]);
  not not_3 (not_3_out, in_1[2]);
  and and_3 (out_2[1], in_1[3], not_3_out, in_1[0]);
  or or_1 (out_2[0], in_1[0], in_1[3]);
endmodule
